# Fritzing sketch plant_monitor (saved by Fritzing 0.9.3b)
breadboards: 1

parts:
  Raspberry_Pi_Zero1 = Raspberry Pi Zero  # not connected
  IC1 = MCP3008 8-channel 10-bit ADC [part_number=MCP3008]
  Pi1 = Adafruit Pi Cobbler
  J1 = screw terminal, 3 pins  # not connected

nets:
  GND: IC1.no_name_yet#9, IC1.no_name_yet#14, Pi1.GND
  N1: IC1.no_name_yet#10, Pi1.CE0
  N2: IC1.no_name_yet#11, Pi1.MOSI
  N3: IC1.no_name_yet#12, Pi1.MISO
  N4: IC1.no_name_yet#13, Pi1.SCLK
  Vcc: IC1.no_name_yet#15, IC1.no_name_yet#16, Pi1.3V3

notes:
  Moisture sensor
  GND - black
  Vcc - Red
  SIG - yellow

custom parts:
  Adafruit Pi Cobbler: Adafruit Pi Cobbler GPIO Breakout for Raspberry Pi
